# Fritzing sketch 2024-09-22 Rotary joystick electric diagram v1.01 (saved by Fritzing 1.0.2b)
circuit board: 5.5cm x 4.5cm
perfboards: 1

parts:
  Arduino_micro_rev3 = Arduino Micro (Rev3)
  J1 = female pin header, 3 pins [form="♀ (female)"]
  J2 = female pin header, 2 pins [form="♀ (female)"]
  J3 = female pin header, 2 pins [form="♀ (female)"]
  J4 = female pin header, 5 pins [form="♀ (female)"]
  J5 = female pin header, 2 pins [form="♀ (female)"]
  J6 = female pin header, 2 pins [form="♀ (female)"]
  J7 = female pin header, 2 pins [form="♀ (female)"]
  J8 = female pin header, 2 pins [form="♀ (female)"]
  LED1 = LED - 5mm [color="Red (633nm)" current=0.030A package="5 mm [THT]"]
  C1 = Electrolytic Capacitor [capacitance=2.2nF voltage=35V package="100 mil [THT, electrolytic]"]
  R1 = Resistor [tolerance=±5% power=0.25W resistance=100 package=THT]
  R3 = Resistor [tolerance=±5% power=0.25W resistance=1k package=THT]
  R2 = Resistor [tolerance=±5% power=0.25W resistance=1k package=THT]
  R4 = Resistor [tolerance=±5% power=0.25W resistance=1k package=THT]
  R5 = Resistor [tolerance=±5% power=0.25W resistance=1k package=THT]
  R6 = Resistor [tolerance=±5% power=0.25W resistance=1k package=THT]
  R7 = Resistor [tolerance=±5% power=0.25W resistance=1k package=THT]
  R8 = Resistor [tolerance=±5% power=0.25W resistance=1k package=THT]
  R9 = Resistor [tolerance=±5% power=0.25W resistance=1k package=THT]
  R10 = Resistor [tolerance=±5% power=0.25W resistance=1k package=THT]
  R11 = Resistor [tolerance=±5% power=0.25W resistance=1k package=THT]
  R12 = Resistor [tolerance=±5% power=0.25W resistance=1k package=THT]
  R13 = Resistor [tolerance=±5% power=0.25W resistance=1k package=THT]
  S1 = Round Pushbutton
  S2 = Round Pushbutton
  S3 = Round Pushbutton
  switch1 = Rotary_Switch_12x1
  S4 = Round Pushbutton
  S5 = Round Pushbutton
  S6 = Round Pushbutton
  JL012-13-5_1 = JL012-13-5.2 Lever (Limit) Switch SPDT + NO + NC [part_number=JL012-13-5.2]
  JL012-13-5_2 = JL012-13-5.2 Lever (Limit) Switch SPDT + NO + NC [part_number=JL012-13-5.2]
  JL012-13-5_4 = JL012-13-5.2 Lever (Limit) Switch SPDT + NO + NC [part_number=JL012-13-5.2]
  JL012-13-5_3 = JL012-13-5.2 Lever (Limit) Switch SPDT + NO + NC [part_number=JL012-13-5.2]

nets:
  GND: Arduino_micro_rev3.GND, J1.pin1, J2.pin2, J3.pin2, J4.pin5, J5.pin1, J6.pin1, J7.pin1, J8.pin1, C1.-, R2.Pin_1, R13.Pin_0, S1.leg0, S2.leg0, S3.leg0, switch1.11, S4.leg0, S5.leg0, S6.leg0, JL012-13-5_1.NC, JL012-13-5_2.NC, JL012-13-5_4.NC, JL012-13-5_3.NC
  N1: Arduino_micro_rev3.D3/SCL, J4.pin4, JL012-13-5_4.C
  N2: Arduino_micro_rev3.D4_PWM/A6, J4.pin3, JL012-13-5_2.C
  N3: Arduino_micro_rev3.D5_PWM, J4.pin2, JL012-13-5_3.C
  N4: Arduino_micro_rev3.D6_PWM/A7, J4.pin1, JL012-13-5_1.C
  button6: Arduino_micro_rev3.D7, J3.pin1, S3.leg1
  button5: Arduino_micro_rev3.D8_PWM/A8, J2.pin1, S2.leg1
  button4: Arduino_micro_rev3.D9_PWM/A9, J8.pin2, S6.leg1
  button3: Arduino_micro_rev3.D10_PWM/A10, J7.pin2, S5.leg1
  button2: Arduino_micro_rev3.D11_PWM, J6.pin2, S4.leg1
  button1: Arduino_micro_rev3.D12_PWM/A11, J5.pin2, S1.leg1
  5V: Arduino_micro_rev3.5V, J1.pin2, LED1.anode, R12.Pin_0, switch1.12
  Vrotation: Arduino_micro_rev3.A5, J1.pin3, R1.Pin_1
  N5: LED1.cathode, R13.Pin_1
  N6: C1.+, R1.Pin_0, switch1.0
  N7: R3.Pin_0, R2.Pin_0, switch1.10
  N8: R3.Pin_1, R4.Pin_0, switch1.9
  N9: R4.Pin_1, R10.Pin_1, switch1.8
  N10: R5.Pin_0, R11.Pin_0, switch1.2
  N11: R5.Pin_1, R6.Pin_0, switch1.3
  N12: R6.Pin_1, R7.Pin_0, switch1.4
  N13: R7.Pin_1, R9.Pin_0, switch1.5
  N14: R8.Pin_0, R9.Pin_1, switch1.6
  N15: R8.Pin_1, R10.Pin_0, switch1.7
  N16: R11.Pin_1, R12.Pin_1, switch1.1

notes:
  rotary switch custom wired like below
  buttons x2
  buttons x4
  directional switches x4
  rotary joystick
  rotation sensor
  Simple led
  by Hippo
  Rotary Joystick
  V1.00

custom parts:
  JL012-13-5.2 Lever (Limit) Switch SPDT + NO + NC: Micro Switch; Model No.: JL012-13.5-2; Actuator Action: Momentary; Actuator Type: Hinge Lever; Contact Configuration: 1NO, 1NC (SPDT) Temperature -25~65℃；Relative humidity: below 85%; Rate Voltage: 125V AC; Rated Current: 1A.
